# Fritzing sketch pi-furby-dc-motor-TB6612-pi (saved by Fritzing 0.9.3b)

parts:
  Raspberry_Pi_Zero_W = Raspberry Pi Zero
  Part1 = Adafruit TB6612 DC and Stepper Motor Driver [part_number="Adafruit #2448"]
  M1 = DC Motor  # not connected

nets:
  N1: Raspberry_Pi_Zero_W.GPIO4, Part1.PWMA
  GND: Raspberry_Pi_Zero_W.GND, Part1.GND
  N2: Raspberry_Pi_Zero_W.GPIO27, Part1.STBY
  N3: Raspberry_Pi_Zero_W.GPIO22, Part1.AIN2
  N4: Raspberry_Pi_Zero_W.GPIO23, Part1.AIN1
  5V: Raspberry_Pi_Zero_W.5V, Part1.VCC

notes:
  TO FURBY BATTERY PACK
  4
  #6 GND
  #4 5V
  #7 GPCLK0
  #13 BCM27
  #15 BCM22
  #16 BCM23
  OEM FURBY DC MOTOR
  ADAFRUIT TB6612 DC MOTOR DRIVER

custom parts:
  Adafruit TB6612 DC and Stepper Motor Driver: Spin two DC motors, step one bi-polar or uni-polar stepper, or fire off two solenoids with 1.2A per channel using the TB6612. These are perhaps better known as "the drivers in our assembled Adafruit Motorshield or Motor HAT." We really like these dual H-bridges, so if you want to control motors without a shield or HAT these are easy to include on any solderless breadboard or perma-proto.
