# Fritzing sketch dc-motors-TB6612-pi (saved by Fritzing 0.9.3b)

parts:
  Raspberry_Pi_Zero/Zero_W = Raspberry Pi Zero
  Part1 = Adafruit TB6612 DC and Stepper Motor Driver [part_number="Adafruit #2448"]
  M2 = DC Motor  # not connected
  M1 = DC Motor  # not connected

nets:
  N1: Raspberry_Pi_Zero/Zero_W.GPIO4, Part1.PWMA
  N2: Raspberry_Pi_Zero/Zero_W.GPIO17, Part1.AIN2
  N3: Raspberry_Pi_Zero/Zero_W.GPIO27, Part1.STBY
  N4: Raspberry_Pi_Zero/Zero_W.GPIO22, Part1.PWMB
  GND: Raspberry_Pi_Zero/Zero_W.GND, Part1.GND
  N5: Raspberry_Pi_Zero/Zero_W.GPIO23, Part1.BIN2
  N6: Raspberry_Pi_Zero/Zero_W.GPIO18, Part1.AIN1
  5V: Raspberry_Pi_Zero/Zero_W.5V, Part1.VCC

notes:
  TO DC MOTOR POWER SOURCE
  4
  #6 GND
  #4 5V
  #7 GPCLK0
  #13 BCM27
  #15 BCM22
  #16 BCM23
  #12 PWM0
  #11 BCM17

custom parts:
  Adafruit TB6612 DC and Stepper Motor Driver: Spin two DC motors, step one bi-polar or uni-polar stepper, or fire off two solenoids with 1.2A per channel using the TB6612. These are perhaps better known as "the drivers in our assembled Adafruit Motorshield or Motor HAT." We really like these dual H-bridges, so if you want to control motors without a shield or HAT these are easy to include on any solderless breadboard or perma-proto.
