# Fritzing sketch pi-fan-controller (saved by Fritzing 0.9.3b)

parts:
  Raspberry_Pi_1 = Raspberry Pi 3 [part_number=RPI-3-V1.2]
  R1 = Resistor [tolerance=±5% resistance=680 package="1206 [SMD]"]
  Q1 = NPN-Transistor [package="TO92 [THT]"]
  M1 = DC Motor

nets:
  N1: Raspberry_Pi_1.GND, Q1.B
  N2: Raspberry_Pi_1.GPIO17, R1.Pin_0
  N3: Raspberry_Pi_1.5V, M1.pin_1
  N4: R1.Pin_1, Q1.C
  N5: Q1.E, M1.pin_2
